# Fritzing sketch Grovey_Slocks_v01 (saved by Fritzing 0.9.3b)

parts:
  Part1 = Genuino 101
  Grove_Buzzer = Grove Buzz
  Grove_Rotary_Angle_Sensor = Grove Rotary Angle Sensor
  Grove_Button = Grove Button
  Grove_RGB_LCD = Grove RGB LCB
  Electric_Imp_(April_Board) = Electric Imp April
  LED_Tactile_Button = LED Tactile Button Breakout v10 [part_number=BOB-10443]
  12V_DC = UK Plug with 2.1mm Barrel Jack
  Grove_Relay2 = Grove Relay
  S1 = Relay_ScrewTerminal
  Electric_Strike_Lock = Electric Strike Lock
  Grove_Light_Sensor = Grove Light Sensor
  Grove_Relay1 = Grove Relay
  S2 = Relay_ScrewTerminal
  12v_G4_LED_BULB = G4 LED spot bulb [package="[THT]"]
  R1 = Resistor [tolerance=±5% resistance=220 package=THT]

nets:
  N1: Part1.A0, Grove_Rotary_Angle_Sensor.SIG
  N2: Part1.A1, Grove_Light_Sensor.SIG
  N3: Part1.A2, LED_Tactile_Button.2
  N4: Part1.A3, LED_Tactile_Button.3
  N5: Part1.A4/SDA, Grove_RGB_LCD.SDA
  N6: Part1.A5/SCL, Grove_RGB_LCD.SCL
  N7: Part1.D8, Grove_Relay2.SIG
  N8: Part1.D3_PWM, Electric_Imp_(April_Board).4
  N9: Part1.D4, Electric_Imp_(April_Board).3
  N10: Part1.D5_PWM, Grove_Relay1.SIG
  N11: Part1.D6_PWM, Grove_Buzzer.SIG
  N12: Part1.D7, Grove_Button.SIG
  VCC: Part1.5V, Grove_Buzzer.VCC, Grove_Rotary_Angle_Sensor.VCC, Grove_Button.VCC, Grove_RGB_LCD.VCC, Grove_Relay2.VCC, Grove_Light_Sensor.VCC, Grove_Relay1.VCC
  GND: Part1.GND, Grove_Buzzer.GND, Grove_Rotary_Angle_Sensor.GND, Grove_Button.GND, Grove_RGB_LCD.GND, Electric_Imp_(April_Board).11, LED_Tactile_Button.1, LED_Tactile_Button.4, 12V_DC.NEG, Grove_Relay2.GND, Electric_Strike_Lock.pin1, Grove_Light_Sensor.GND, Grove_Relay1.GND, 12v_G4_LED_BULB.cathode
  N13: Part1.VIN, Electric_Imp_(April_Board).10, 12V_DC.POS, S1.leg1, S2.leg0
  N14: S1.leg0, Electric_Strike_Lock.pin2
  N15: S2.leg1, R1.Pin_0
  N16: 12v_G4_LED_BULB.anode, R1.Pin_1

custom parts:
  Genuino 101: A learning and development board that delivers the performance and low-power consumption of the Intel® Curie™ Module with the simplicity of Arduino at an entry-level price. It keeps the same robust form factor and peripheral list of the UNO with the addition of onboard Bluetooth LE capabilities and a 6-axis accelerometer/gyro to help you easily expand your creativity into the connected world.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
  Grove Rotary Angle Sensor: A potentiometer
  Grove RGB LCB: Grove RGB LCD
  Electric Imp April: Electric Imp Breakout Board with onboard 3.3V regulated power supply
  LED Tactile Button Breakout v10: This simple breakout board makes it easy to use our LED tactile switches in a breadboard, or your next project.
  Grove Relay: Relay, Grove connector.
  Relay_ScrewTerminal: Generic Relay Screw Terminal
  G4 LED spot bulb: RS Components G4 LED spot bulb: 1W LED lamp, AC/DC 12V input voltage
